# Fritzing sketch SM-CON-REV4-161019 (saved by Fritzing 0.9.3b)
circuit board: 10.3cm x 12cm
breadboards: 1

parts:
  WIZ820io = WIZ820io [part_number=WIZ820io]
  J7 = screw terminal, 2 pins
  R20 = Resistor [tolerance=±5% resistance=100 package="1206 [SMD]"]
  R19 = Resistor [tolerance=±5% resistance=100 package="1206 [SMD]"]
  R18 = Resistor [tolerance=±5% resistance=100 package="1206 [SMD]"]
  R17 = Resistor [tolerance=±5% resistance=100 package="1206 [SMD]"]
  R16 = Resistor [tolerance=±5% resistance=100 package="1206 [SMD]"]
  R15 = Resistor [tolerance=±5% resistance=100 package="1206 [SMD]"]
  R9 = Resistor [tolerance=±5% resistance=100 package="1206 [SMD]"]
  R10 = Resistor [tolerance=±5% resistance=100 package="1206 [SMD]"]
  R11 = Resistor [tolerance=±5% resistance=100 package="1206 [SMD]"]
  R12 = Resistor [tolerance=±5% resistance=100 package="1206 [SMD]"]
  R13 = Resistor [tolerance=±5% resistance=100 package="1206 [SMD]"]
  R8 = Resistor [tolerance=±5% resistance=100 package="1206 [SMD]"]
  R7 = Resistor [tolerance=±5% resistance=100 package="1206 [SMD]"]
  R14 = Resistor [tolerance=±5% resistance=100 package="1206 [SMD]"]
  IC1 = 74HC4051 [package=so16]
  J5 = prefix0000 [form="♂ (shrouded male)"]
  IC3 = CD74HCT245
  IC2 = CD74HCT245
  R2 = Resistor [tolerance=±5% resistance=10k package="1206 [SMD]"]
  C1 = Ceramic Capacitor [capacitance=0.1µF package="1206 [SMD, multilayer]"]
  R1 = Resistor [tolerance=±5% resistance=10k package="1206 [SMD]"]
  R4 = Resistor [tolerance=±5% resistance=10k package="1206 [SMD]"]
  R5 = Resistor [tolerance=±5% resistance=10k package="1206 [SMD]"]
  R6 = Resistor [tolerance=±5% resistance=10k package="1206 [SMD]"]
  R3 = Resistor [tolerance=±5% resistance=10k package="1206 [SMD]"]
  J6 = prefix0000
  U1 = prefix0000 [chip_label="DIP SWITCH"]
  J1 = prefix0000 [form="♂ (male)"]
  J3 = MURATA_OKI-78SR
  R21 = prefix0000
  J8 = prefix0000 [form="♀ (female)"]
  J9 = prefix0000 [form="♀ (female)"]

nets (from the pcb view):
  N1: WIZ820io.MOSI, J9.connector12
  N2: WIZ820io.SCLK, J8.connector13
  N3: WIZ820io.nSS, J9.connector11
  N4: WIZ820io.MISO, J9.connector13
  N5: WIZ820io.nRESET, IC1.IO6
  N6: WIZ820io.VIN, J8.connector2
  N7: J7.pin1, J5.connector0, J5.connector1, J5.connector2, J5.connector3, J5.connector5, J5.connector7, J5.connector9, J5.connector11, J6.connector0, J6.connector1, J6.connector2, J6.connector4, J6.connector6, J6.connector8, J1.connector0, J3.connector2
  N8: R20.Pin_0, IC3.connector18
  N9: R20.Pin_1, J6.connector14
  N10: R19.Pin_0, IC3.connector17
  N11: R19.Pin_1, J6.connector13
  N12: R18.Pin_0, IC3.connector15
  N13: R18.Pin_1, J6.connector12
  N14: R17.Pin_0, IC3.connector14
  N15: R17.Pin_1, J6.connector11
  N16: R16.Pin_0, IC3.connector13
  N17: R16.Pin_1, J6.connector10
  N18: R15.Pin_0, IC3.connector12
  N19: R15.Pin_1, J6.connector9
  N20: R9.Pin_0, IC2.connector12
  N21: R9.Pin_1, J5.connector14
  N22: R10.Pin_0, IC2.connector13
  N23: R10.Pin_1, J5.connector15
  N24: R11.Pin_0, IC2.connector14
  N25: R11.Pin_1, J5.connector16
  N26: R12.Pin_0, IC2.connector15
  N27: R12.Pin_1, J5.connector17
  N28: R13.Pin_0, IC2.connector17
  N29: R13.Pin_1, J5.connector18
  N30: R8.Pin_0, IC2.connector11
  N31: R8.Pin_1, J5.connector13
  N32: R7.Pin_0, IC2.connector10
  N33: R7.Pin_1, J5.connector12
  N34: R14.Pin_0, IC2.connector18
  N35: R14.Pin_1, J5.connector19
  N36: IC1.IO4, R6.Pin_1, U1.connector4
  N37: IC1.IO, J8.connector3
  N38: IC1.IO7, R21.connector1
  N39: IC1.INH, R1.Pin_1
  N40: IC1.C, J8.connector4
  N41: IC1.B, J8.connector5
  N42: IC1.A, J8.connector6
  N43: IC1.IO3, R2.Pin_1, U1.connector0
  N44: IC1.IO0, R3.Pin_1, U1.connector1
  N45: IC1.IO1, R4.Pin_1, U1.connector2
  N46: IC1.IO2, R5.Pin_1, U1.connector3
  N47: IC1.VDD, IC3.connector0, IC3.connector20, IC2.connector0, IC2.connector20, C1.1, U1.connector5, U1.connector6, U1.connector7, U1.connector8, U1.connector9, J3.connector1, R21.connector2, J8.connector0
  N48: J5.connector4, J5.connector6, J5.connector8, J5.connector10, J5.connector20
  N49: IC3.connector1, J8.connector7
  N50: IC3.connector2, J8.connector8
  N51: IC3.connector3, J8.connector9
  N52: IC3.connector4, J8.connector10
  N53: IC3.connector5, J8.connector11
  N54: IC3.connector6, J8.connector12
  N55: IC2.connector1, J9.connector10
  N56: IC2.connector2, J9.connector9
  N57: IC2.connector3, J9.connector8
  N58: IC2.connector4, J9.connector7
  N59: IC2.connector5, J9.connector6
  N60: IC2.connector6, J9.connector5
  N61: IC2.connector7, J9.connector4
  N62: IC2.connector8, J9.connector3
  N63: R2.Pin_0, R4.Pin_0, R5.Pin_0, R6.Pin_0, R3.Pin_0
  N64: J6.connector3, J6.connector5, J6.connector7, J6.connector15
  N65: R21.connector0, J8.connector1

notes:
  VER 2.0 OCT 2014
  5V
  CONNECTIVE TISSUE, CONTROLLER PCB, 4
  12V
  GND
  CONTROLLER BOARD
  RC+
  161019 REV4
  7SIG 32ADD
  TEENSY 3.2
  USB
  12V FAN
  +
  -
  BRIGHTNESS
  ADJUSTMENT
  ADDRESS
  OKI-78SR
